// Logisim project Controller.circ as structural Verilog: 7 circuits, main circuit Controller
module Controller (
  input  [15:0] Inst,
  input  [3:0] Flags,
  input  Reset,
  input  Clk,
  output Carry,
  output DP_Shift,
  output Move,
  output [4:0] Imm5,
  output [7:0] Imm8,
  output [3:0] ALU_Opcode,
  output [2:0] Rm,
  output [2:0] Rn,
  output [2:0] Rd,
  output [31:0] RAM_Addr,
  output Load,
  output Store,
  output [7:0] PC
);

  wire conditional_1_verified, opcode_decoder_1_branch, opcode_decoder_1_data_processing,
       opcode_decoder_1_load_store, opcode_decoder_1_shift, opcode_decoder_1_sp_address,
       shift_add_sub_mov_1_carry, sp_address_1_write_enable;
  wire [2:0] data_processing_1_rd, data_processing_1_rm, data_processing_1_rn, load_store_1_rd,
       load_store_1_rm, load_store_1_rn, shift_add_sub_mov_1_rd, shift_add_sub_mov_1_rm,
       shift_add_sub_mov_1_rn;
  wire [3:0] data_processing_1_alu_opcode, shift_add_sub_mov_1_alu_opcode;
  wire [7:0] adder_1_out, adder_2_out, conditional_1_offset;
  wire [31:0] sp_address_1_new_stack_pointer, Stack_Pointer_q;

  Register #(.width(32)) Stack_Pointer (
    .D(sp_address_1_new_stack_pointer), .en(sp_address_1_write_enable), .clk(Clk), .Q(Stack_Pointer_q),
    .clr(Reset));
  Opcode_Decoder opcode_decoder_1 (
    .Opcode(Inst[15:10]), .Shift(opcode_decoder_1_shift), .Data_Processing(opcode_decoder_1_data_processing),
    .Load_Store(opcode_decoder_1_load_store), .SP_Address(opcode_decoder_1_sp_address),
    .Branch(opcode_decoder_1_branch));
  Shift_Add_Sub_Mov shift_add_sub_mov_1 (
    .Rm(shift_add_sub_mov_1_rm), .ALU_Opcode(shift_add_sub_mov_1_alu_opcode), .Move(Move),
    .Instruction(Inst), .Rd(shift_add_sub_mov_1_rd), .Imm5(Imm5), .Rn(shift_add_sub_mov_1_rn), .Imm8(Imm8),
    .Enable(opcode_decoder_1_shift), .Carry(shift_add_sub_mov_1_carry));
  Data_Processing data_processing_1 (
    .Instruction(Inst), .ALU_Opcode(data_processing_1_alu_opcode), .Enable(opcode_decoder_1_data_processing),
    .Rm(data_processing_1_rm), .Rn(data_processing_1_rn), .Rd(data_processing_1_rd));
  Load_Store load_store_1 (
    .Rn(load_store_1_rn), .Stack_Pointer(Stack_Pointer_q), .Instruction(Inst), .Rm(load_store_1_rm),
    .Store(Store), .Enable(opcode_decoder_1_load_store), .Load(Load), .Rd(load_store_1_rd),
    .RAM_Addr(RAM_Addr));
  Conditional conditional_1 (
    .Offset(conditional_1_offset), .Z(Flags[1]), .Instruction(Inst), .C(Flags[2]), .V(Flags[3]),
    .Enable(opcode_decoder_1_branch), .N(Flags[0]), .Verified(conditional_1_verified));
  SP_Address sp_address_1 (
    .New_Stack_Pointer(sp_address_1_new_stack_pointer), .Enable(opcode_decoder_1_sp_address),
    .Write_Enable(sp_address_1_write_enable), .Instruction(Inst), .Stack_Pointer(Stack_Pointer_q));
  Adder adder_1 (.a(8'h3), .b(conditional_1_offset), .out(adder_1_out));  // open: cin, cout
  Adder adder_2 (.a(adder_1_out), .b(PC), .out(adder_2_out));  // open: cin, cout
  and and_1 (DP_Shift, opcode_decoder_1_shift, ~opcode_decoder_1_data_processing);  // AND_Gate
  Counter counter_1 (
    .clr(Reset), .load(conditional_1_verified), .up(1'b1), .count(1'b1), .clk(Clk), .D(adder_2_out), .Q(PC));  // open: carry
  Multiplexer #(.enable("false")) multiplexer_1 (
    .in0(Flags[2]), .in1(shift_add_sub_mov_1_carry), .out(Carry), .sel(DP_Shift));
  assign ALU_Opcode = shift_add_sub_mov_1_alu_opcode | data_processing_1_alu_opcode;  // OR_Gate or_1, 4 bits wide
  assign Rm = shift_add_sub_mov_1_rm | data_processing_1_rm | load_store_1_rm;  // OR_Gate or_2, 3 bits wide
  assign Rn = shift_add_sub_mov_1_rn | data_processing_1_rn | load_store_1_rn;  // OR_Gate or_3, 3 bits wide
  assign Rd = shift_add_sub_mov_1_rd | data_processing_1_rd | load_store_1_rd;  // OR_Gate or_4, 3 bits wide

  // Notes on the sheet:
  //   Extract carry
  //   Extract Opcode
  //   IF Reg_Imm=1 THEN use shift value from register ELSE use shift value from Imm5
  //   Add 3 to offset because ARM pre-increments PC
  //   and does an additionnal prefect operation
  //   TODO: handle SUB case
endmodule

module Conditional (
  input  Enable,
  input  [15:0] Instruction,
  input  Z,
  input  V,
  input  N,
  input  C,
  output [7:0] Offset,
  output Verified
);

  wire and_1_out, and_2_out, and_3_out, and_4_out, and_5_out, and_6_out, and_7_out, and_8_out, and_9_out,
       and_10_out, and_11_out, and_12_out, decoder_1_out0, decoder_1_out1, decoder_1_out2, decoder_1_out3,
       decoder_1_out4, decoder_1_out5, decoder_1_out6, decoder_1_out7, decoder_1_out8, decoder_1_out9,
       decoder_1_out10, decoder_1_out11, decoder_1_out12, decoder_1_out13, decoder_1_out14,
       multiplexer_1_out, nand_1_out, nand_2_out, nand_3_out, nand_4_out, or_1_out, or_2_out, xnor_1_out,
       xnor_2_out, xor_1_out, xor_2_out;

  Decoder #(.select(4), .enable("false")) decoder_1 (
    .out0(decoder_1_out0), .out1(decoder_1_out1), .out2(decoder_1_out2), .out3(decoder_1_out3),
    .out4(decoder_1_out4), .out5(decoder_1_out5), .out6(decoder_1_out6), .out7(decoder_1_out7),
    .out8(decoder_1_out8), .out9(decoder_1_out9), .out10(decoder_1_out10), .out11(decoder_1_out11),
    .out12(decoder_1_out12), .out13(decoder_1_out13), .out14(decoder_1_out14), .sel(Instruction[11:8]));  // open: out15
  xor xor_1 (xor_1_out, N, V);
  xor xor_2 (xor_2_out, V, N);
  and and_1 (and_1_out, Z, decoder_1_out0);
  nand nand_1 (nand_1_out, Z, decoder_1_out1);
  and and_2 (and_2_out, C, decoder_1_out2);
  nand nand_2 (nand_2_out, C, decoder_1_out3);
  and and_3 (and_3_out, N, decoder_1_out4);
  nand nand_3 (nand_3_out, N, decoder_1_out5);
  and and_4 (and_4_out, V, decoder_1_out6);
  nand nand_4 (nand_4_out, V, decoder_1_out7);
  and and_5 (and_5_out, ~Z, C);  // AND_Gate
  or or_1 (or_1_out, ~C, Z);  // OR_Gate
  xnor xnor_1 (xnor_1_out, N, V);
  and and_6 (and_6_out, ~Z, xnor_2_out);  // AND_Gate
  xnor xnor_2 (xnor_2_out, V, N);
  or or_2 (or_2_out, Z, ~xor_2_out);  // OR_Gate
  and and_7 (and_7_out, and_5_out, decoder_1_out8);
  and and_8 (and_8_out, or_1_out, decoder_1_out9);
  and and_9 (and_9_out, xnor_1_out, decoder_1_out10);
  and and_10 (and_10_out, ~xor_1_out, decoder_1_out11);  // AND_Gate
  and and_11 (and_11_out, and_6_out, decoder_1_out12);
  and and_12 (and_12_out, or_2_out, decoder_1_out13);
  Multiplexer #(.select(4)) multiplexer_1 (
    .in0(and_1_out), .in1(nand_1_out), .in2(and_2_out), .in3(nand_2_out), .in4(and_3_out), .in5(nand_3_out),
    .in6(and_4_out), .in7(nand_4_out), .in8(and_7_out), .in9(and_8_out), .in10(and_9_out), .in11(and_10_out),
    .in12(and_11_out), .in13(and_12_out), .in14(decoder_1_out14), .out(multiplexer_1_out),
    .sel(Instruction[11:8]));  // open: in15, en
  and and_13 (Verified, Enable, multiplexer_1_out);

  assign Offset = Instruction[7:0];
endmodule

module Opcode_Decoder (
  input  [5:0] Opcode,
  output Shift,
  output Data_Processing,
  output Load_Store,
  output SP_Address,
  output Branch
);

  wire Immediat8;

  and and_1 (Shift, ~Opcode[5], ~Opcode[4]);  // AND_Gate
  and and_2 (Data_Processing, ~Opcode[5], Opcode[4], ~Opcode[3], ~Opcode[2], ~Opcode[1], ~Opcode[0]);  // AND_Gate
  and and_3 (Load_Store, Opcode[5], ~Opcode[4], ~Opcode[3], Opcode[2]);  // AND_Gate
  and and_4 (SP_Address, Opcode[5], ~Opcode[4], Opcode[3], Opcode[2]);  // AND_Gate
  and and_5 (Immediat8, Opcode[5], Opcode[4], Opcode[3], ~Opcode[2], ~Opcode[1]);  // AND_Gate
  and and_6 (Branch, Opcode[5], Opcode[4], ~Opcode[3], Opcode[2]);  // AND_Gate

  // Notes on the sheet:
  //   Shift, add, sub, mov
  //   Data Processing
  //   Load/Store
  //   WTF?
  //   Branch
endmodule

module Data_Processing (
  input  [15:0] Instruction,
  input  Enable,
  output [2:0] Rn,
  output [2:0] Rd,
  output [2:0] Rm,
  output [3:0] ALU_Opcode
);

  wire [15:0] bit_extender_1_out;
  wire [15:10] and_1_out;

  assign bit_extender_1_out = {{15{Enable}}, Enable};  // Bit_Extender bit_extender_1
  assign {and_1_out, ALU_Opcode, Rm, Rd} = Instruction & bit_extender_1_out;  // AND_Gate and_1, 16 bits wide

  assign Rn = Rd;

  // Notes on the sheet:
  //   Note 2: RSB instruction has Rn as 1st operand.
  //   Pull output low on Enable = 0
  //   MUL instruction has Rn as 1st operand and Rdm as 2nd operand
  //   For simplification purposes, Rm is used for 1st operand both here and in the ALU.
  //   Discard instruction Opcode
  //   Extract arguments
  //   Note: instructions that does not save the result will still have the second operand as the destination register, the ALU will copy the second register to the destination register
endmodule

module Shift_Add_Sub_Mov (
  input  Enable,
  input  [15:0] Instruction,
  output [3:0] ALU_Opcode,
  output Carry,
  output Move,
  output [2:0] Rd,
  output [2:0] Rn,
  output [2:0] Rm,
  output [4:0] Imm5,
  output [7:0] Imm8
);

  wire and_2_out, and_3_out, and_4_out, and_5_out, and_6_out;
  wire [2:0] priority_encoder_1_out;
  wire [3:0] bit_extender_1_out, multiplexer_6_out;
  wire [15:0] and_1_out, bit_extender_2_out;

  assign bit_extender_1_out = {{3{Enable}}, Enable};  // Bit_Extender bit_extender_1
  assign bit_extender_2_out = {{15{Enable}}, Enable};  // Bit_Extender bit_extender_2
  assign and_1_out = bit_extender_2_out & Instruction;  // AND_Gate and_1, 16 bits wide
  and and_2 (and_2_out, ~and_1_out[13], ~and_1_out[12], ~and_1_out[11]);  // AND_Gate
  and and_3 (and_3_out, ~and_1_out[13], ~and_1_out[12], and_1_out[11]);  // AND_Gate
  and and_4 (and_4_out, ~and_1_out[13], and_1_out[12], ~and_1_out[11]);  // AND_Gate
  and and_5 (and_5_out, ~and_1_out[13], and_1_out[12], and_1_out[11], ~and_1_out[10], ~and_1_out[9]);  // AND_Gate
  and and_6 (and_6_out, ~and_1_out[13], and_1_out[12], and_1_out[11], ~and_1_out[10], and_1_out[9]);  // AND_Gate
  and and_7 (Move, and_1_out[13], ~and_1_out[12], ~and_1_out[11]);  // AND_Gate
  Multiplexer #(.select(3), .width(3), .enable("false")) multiplexer_1 (
    .in0(and_1_out[2:0]), .in1(and_1_out[2:0]), .in2(and_1_out[2:0]), .in3(and_1_out[2:0]),
    .in4(and_1_out[2:0]), .in5(and_1_out[10:8]), .in6(3'b000), .in7(3'b000), .out(Rd),
    .sel(priority_encoder_1_out));
  Multiplexer #(.select(3), .width(3), .enable("false")) multiplexer_2 (
    .in0(and_1_out[5:3]), .in1(and_1_out[5:3]), .in2(and_1_out[5:3]), .in3(and_1_out[5:3]),
    .in4(and_1_out[5:3]), .in5(3'b000), .in6(3'b000), .in7(3'b000), .out(Rn), .sel(priority_encoder_1_out));
  Multiplexer #(.select(3), .width(3), .enable("false")) multiplexer_3 (
    .in0(3'b000), .in1(3'b000), .in2(3'b000), .in3(and_1_out[8:6]), .in4(and_1_out[8:6]), .in5(3'b000),
    .in6(3'b000), .in7(3'b000), .out(Rm), .sel(priority_encoder_1_out));
  Multiplexer #(.select(3), .width(5), .enable("false")) multiplexer_4 (
    .in0(and_1_out[10:6]), .in1(and_1_out[10:6]), .in2(and_1_out[10:6]), .in3({5{1'b0}}), .in4({5{1'b0}}),
    .in5({5{1'b0}}), .in6({5{1'b0}}), .in7({5{1'b0}}), .out(Imm5), .sel(priority_encoder_1_out));
  Multiplexer #(.select(3), .width(8), .enable("false")) multiplexer_5 (
    .in0({8{1'b0}}), .in1({8{1'b0}}), .in2({8{1'b0}}), .in3({8{1'b0}}), .in4({8{1'b0}}),
    .in5(and_1_out[7:0]), .in6({8{1'b0}}), .in7({8{1'b0}}), .out(Imm8), .sel(priority_encoder_1_out));
  Priority_Encoder priority_encoder_1 (
    .in0(and_2_out), .in1(and_3_out), .in2(and_4_out), .in3(and_5_out), .in4(and_6_out), .in5(Move),
    .in6(1'b0), .in7(1'b0), .out(priority_encoder_1_out));  // open: en_in, gs, en_out
  Multiplexer #(.select(3), .width(4), .enable("false")) multiplexer_6 (
    .in0(4'b0010), .in1(4'b0011), .in2(4'b0100), .in3(4'b0101), .in4(4'b0110), .in5(4'b0000), .in6(4'b0000),
    .in7(4'b0000), .out(multiplexer_6_out), .sel(priority_encoder_1_out));
  Multiplexer #(.select(3), .enable("false")) multiplexer_7 (
    .in0(1'b0), .in1(1'b0), .in2(1'b0), .in3(1'b0), .in4(1'b1), .in5(1'b0), .in6(1'b0), .in7(1'b0),
    .out(Carry), .sel(priority_encoder_1_out));
  assign ALU_Opcode = bit_extender_1_out & multiplexer_6_out;  // AND_Gate and_8, 4 bits wide

  // Notes on the sheet:
  //   Pull output low on Enable = 0
  //   Note: ALU uses Rn register for shifts. Use Rn instead of Rm for shifts (immediate) here too
  //   Note 2: Move output indicates a MOV instruction for the CPU to select the Imm8 as input for the destination register Rd
  //   Extract lower level opcode
  //   Rd
  //   Rd_MOV
  //   Rm_Shift / Rn_Add_Sub
  //   Rm_Add_Sub
  //   Imm5
  //   Imm8
  //   LSL 0010
  //   LSR 0011
  //   ASR 0100
  //   ADD 0101
  //   SUB 0110
  //   MOV
  //   Select correct bits for Rd
  //   Inhibit Rn selection for move
  //   Inhibit Rm selection for shift/move
  //   Inhibit Imm5 for add/sub/move
  //   Inhibit Imm8 for shift/add/sub
  //   Select ALU Opcode for Shift/Add/Sub
  //   Enable carry for SUB since it is reversed in ALU
endmodule

module Load_Store (
  input  Enable,
  input  [15:0] Instruction,
  input  [31:0] Stack_Pointer,
  output Store,
  output Load,
  output [2:0] Rm,
  output [2:0] Rn,
  output [2:0] Rd,
  output [31:0] RAM_Addr
);

  wire [15:0] and_1_out, bit_extender_1_out;
  wire [31:0] adder_1_out, bit_extender_2_out, bit_extender_3_out;

  assign bit_extender_1_out = {{15{Enable}}, Enable};  // Bit_Extender bit_extender_1
  assign {and_1_out[15:12], Load, Rd, and_1_out[7:0]} = Instruction & bit_extender_1_out;  // AND_Gate and_1, 16 bits wide
  assign bit_extender_2_out = {{24{and_1_out[7]}}, and_1_out[7:0]};  // Bit_Extender bit_extender_2
  assign bit_extender_3_out = {{31{Enable}}, Enable};  // Bit_Extender bit_extender_3
  Adder #(.width(32)) adder_1 (.a(bit_extender_2_out), .b(Stack_Pointer), .out(adder_1_out));  // open: cin, cout
  and and_2 (Store, Enable, ~Load);  // AND_Gate
  assign RAM_Addr = adder_1_out & bit_extender_3_out;  // AND_Gate and_3, 32 bits wide

  assign Rm = Rd;
  assign Rn = Rd;
endmodule

module SP_Address (
  input  Enable,
  input  [15:0] Instruction,
  input  [31:0] Stack_Pointer,
  output Write_Enable,
  output [31:0] New_Stack_Pointer
);

  wire and_2_out;
  wire [15:0] and_1_out, bit_extender_1_out;
  wire [31:0] adder_1_out, bit_extender_2_out, subtractor_1_out;

  assign bit_extender_1_out = {{15{Enable}}, Enable};  // Bit_Extender bit_extender_1
  assign and_1_out = bit_extender_1_out & Instruction;  // AND_Gate and_1, 16 bits wide
  assign bit_extender_2_out = {{25{1'b0}}, and_1_out[6:0]};  // Bit_Extender bit_extender_2
  and and_2 (and_2_out, ~and_1_out[8], ~and_1_out[9], ~and_1_out[10], ~and_1_out[11]);  // AND_Gate
  Adder #(.width(32)) adder_1 (.a(Stack_Pointer), .b(bit_extender_2_out), .out(adder_1_out));  // open: cin, cout
  Subtractor #(.width(32)) subtractor_1 (
    .a(Stack_Pointer), .b(bit_extender_2_out), .out(subtractor_1_out));  // open: bin, bout
  Multiplexer #(.width(32), .enable("false")) multiplexer_1 (
    .in0(adder_1_out), .in1(subtractor_1_out), .out(New_Stack_Pointer), .sel(and_1_out[7]));
  and and_3 (Write_Enable, Enable, and_2_out);

  // Notes on the sheet:
  //   Pull output low on Enable = 0
  //   Check miscellaneous 16-bit instructions opcode
  //   ADD or SUB
endmodule
