// Logisim project Machine_Logisim3.circ as structural Verilog: 3 circuits, main circuit Facade
module Facade (
);

  wire and_1_out, and_2_out, and_3_out, and_4_out, and_5_out, and_6_out, BREAK, Clk, Clk_Button2,
       Clk_Button_out, clock_1_out, CONTINUE, d_ff_2_qn, decoder_1_out0, decoder_1_out1, decoder_1_out2,
       decoder_1_out3, decoder_1_out4, decoder_1_out5, KEYB_Eof, KEYB_Read, KEYB_ReadEn, MMIO_En, or_1_out,
       or_4_out, Reset, RNG_Read, Rst_Button_out, RST_Signal, Store, TTY_Upd;
  wire [3:0] binary_to_bcd_converter_1_p2, binary_to_bcd_converter_1_p3, binary_to_bcd_converter_1_p4,
       binary_to_bcd_converter_1_p5, CPU_1_flags, MMIO_Addr;
  wire [4:0] JOY_X, JOY_Y;
  wire [6:0] KEYB_Char, TTY_Char;
  wire [7:4] RAM_Addr;
  wire [15:0] multiplier_1_out, ROM_Addr, ROMa_data;
  wire [31:0] bcd8digits_1_bcd, CPU_1_r0, CPU_1_r1, CPU_1_r2, CPU_1_r3, CPU_1_r6, CPU_1_r7, CPU_1_sp, Dip1,
       Dip2, Dip3, divider_1_out, divider_1_rem, MMIO_Out, multiplexer_1_out, R4, R5, RAM_Out, RAMa_dout,
       random_1_out, register_3_q, Res, Screen;
  wire [31:1] undriven_2;
  wire [31:5] undriven_4, undriven_5;
  wire [31:7] undriven, undriven_3;
  wire [31:9] CPU_1_ram_addr;

  DipSwitch dipswitch_1 (
    .sw1(Dip1[7]), .sw2(Dip1[6]), .sw3(Dip1[5]), .sw4(Dip1[4]), .sw5(Dip1[3]), .sw6(Dip1[2]), .sw7(Dip1[1]),
    .sw8(Dip1[0]));
  // Probe on Dip1[7:0]
  DipSwitch dipswitch_2 (
    .sw1(Dip2[7]), .sw2(Dip2[6]), .sw3(Dip2[5]), .sw4(Dip2[4]), .sw5(Dip2[3]), .sw6(Dip2[2]), .sw7(Dip2[1]),
    .sw8(Dip2[0]));
  Keyboard keyboard_1 (.clk(Clk), .re(KEYB_ReadEn), .clr(Reset), .avail(KEYB_Eof), .data(KEYB_Char));
  and and_1 (and_1_out, MMIO_En, Store);
  Decoder #(.select(4)) decoder_1 (
    .out0(decoder_1_out0), .out1(decoder_1_out1), .out2(decoder_1_out2), .out3(decoder_1_out3),
    .out4(decoder_1_out4), .out5(decoder_1_out5), .sel(MMIO_Addr), .en(and_1_out));  // open: out6, out7, out8, out9, out10, out11, out12, out13, out14, out15
  RAM #(.dataWidth(32)) RAMa (
    .addr({RAM_Addr, MMIO_Addr}), .we(and_2_out), .oe(1'b1), .clk(Clk), .din(RAM_Out), .dout(RAMa_dout));
  and and_2 (and_2_out, ~MMIO_En, Store);  // AND_Gate
  // Probe on Dip2[7:0]
  // Probe on MMIO_Addr
  // Probe on {MMIO_En, RAM_Addr, MMIO_Addr}
  // Probe on Dip3[7:0]
  DipSwitch dipswitch_3 (
    .sw1(Dip3[7]), .sw2(Dip3[6]), .sw3(Dip3[5]), .sw4(Dip3[4]), .sw5(Dip3[3]), .sw6(Dip3[2]), .sw7(Dip3[1]),
    .sw8(Dip3[0]));
  Joystick #(.bits(5)) joystick_1 (.x(JOY_X), .y(JOY_Y));
  Register #(.trigger("falling"), .width(7)) register_1 (
    .D(RAM_Out[6:0]), .en(decoder_1_out0), .clk(Clk), .Q(TTY_Char), .clr(Reset));
  Register #(.width(32)) register_2 (.D(RAM_Out), .en(decoder_1_out1), .clk(Clk), .Q(Res), .clr(Reset));
  Register #(.width(32)) register_3 (.D(RAM_Out), .en(decoder_1_out2), .clk(Clk), .Q(register_3_q), .clr(Reset));
  Register #(.width(1)) register_4 (.D(RAM_Out[0]), .en(decoder_1_out4), .clk(Clk), .Q(RST_Signal), .clr(Reset));
  Register #(.width(1)) register_5 (.D(RAM_Out[0]), .en(decoder_1_out5), .clk(Clk), .Q(BREAK), .clr(or_1_out));
  or or_1 (or_1_out, Reset, CONTINUE);
  Clock clock_1 (.out(clock_1_out));
  DotMatrix #(.inputtype("row"), .matrixcols(8), .matrixrows(4)) dotmatrix_1 (
    .row0(Screen[7:0]), .row1(Screen[15:8]), .row2(Screen[23:16]), .row3(Screen[31:24]));
  D_Flip_Flop d_ff_1 (.D(decoder_1_out0), .clk(Clk), .Q(TTY_Upd));  // open: Qn, preset, reset
  Register #(.width(32)) register_6 (.D(register_3_q), .en(and_3_out), .clk(Clk), .Q(Screen), .clr(Reset));
  and and_3 (and_3_out, RAM_Out[0], decoder_1_out3);
  or or_2 (Clk, and_4_out, Clk_Button_out, Clk_Button2);
  and and_4 (and_4_out, clock_1_out, ~BREAK);  // AND_Gate
  Button Clk_Button (.out(Clk_Button_out));
  Button Rst_Button (.out(Rst_Button_out));
  ROM #(.addrWidth(16), .dataWidth(16)) ROMa (.addr(ROM_Addr), .data(ROMa_data));
  or or_3 (Reset, Rst_Button_out, RST_Signal);
  // Probe on RAMa_dout
  Hex_Digit_Display hex_digit_display_1 (.value(Res[15:12]));  // open: dp
  D_Flip_Flop #(.trigger("falling")) d_ff_2 (.D(1'b0), .clk(Clk), .Qn(d_ff_2_qn), .preset(Reset));  // open: Q, reset
  DotMatrix #(.inputtype("row"), .matrixcols(32), .matrixrows(1)) dotmatrix_2 (.row0(Res));
  Hex_Digit_Display hex_digit_display_2 (.value(Res[11:8]));  // open: dp
  Hex_Digit_Display hex_digit_display_3 (.value(Res[7:4]));  // open: dp
  D_Flip_Flop d_ff_3 (.D(KEYB_Read), .clk(Clk), .Q(KEYB_ReadEn), .reset(or_4_out));  // open: Qn, preset
  or or_4 (or_4_out, ~KEYB_Read, Reset);  // OR_Gate
  Multiplexer #(.enable("false"), .width(32)) multiplexer_1 (
    .in0(RAMa_dout), .in1(MMIO_Out), .out(multiplexer_1_out), .sel(MMIO_En));
  // Probe on multiplexer_1_out
  Button button_1 (.out(CONTINUE));
  Hex_Digit_Display hex_digit_display_4 (.value(Res[3:0]));  // open: dp
  // Probe on CPU_1_r1
  // Probe on CPU_1_r0
  and and_5 (and_5_out, Clk, d_ff_2_qn);
  Hex_Digit_Display hex_digit_display_5 (.value(binary_to_bcd_converter_1_p2));  // open: dp
  // Binary_to_BCD_converter #(.binvalue(13)) binary_to_bcd_converter_1: pin names not known; wires that end beside it: Res[12:0], binary_to_bcd_converter_1_p2, binary_to_bcd_converter_1_p3, binary_to_bcd_converter_1_p4, binary_to_bcd_converter_1_p5
  // Probe on CPU_1_r3
  // Probe on CPU_1_r2
  // Probe on R5
  // Probe on R4
  Button button_2 (.out(Clk_Button2));
  // Probe on Res
  Hex_Digit_Display hex_digit_display_6 (.value(binary_to_bcd_converter_1_p3));  // open: dp
  Hex_Digit_Display hex_digit_display_7 (.value(binary_to_bcd_converter_1_p4));  // open: dp
  Random #(.width(32)) random_1 (.next(RNG_Read), .clk(Clk), .out(random_1_out));  // open: clr
  // Probe on CPU_1_r7
  // Probe on CPU_1_r6
  // Probe on CPU_1_flags
  CPU CPU_1 (
    .Flags(CPU_1_flags), .SP(CPU_1_sp), .RAM_Out(RAM_Out), .ROM_Addr(ROM_Addr), .Store(Store),
    .RAM_Addr({CPU_1_ram_addr, MMIO_En, RAM_Addr, MMIO_Addr}), .R0(CPU_1_r0), .R1(CPU_1_r1), .R2(CPU_1_r2),
    .R3(CPU_1_r3), .R4(R4), .R5(R5), .R6(CPU_1_r6), .R7(CPU_1_r7), .RAM_In(multiplexer_1_out),
    .ROM_In(ROMa_data), .Clk(and_5_out), .Reset(Reset));
  Hex_Digit_Display hex_digit_display_8 (.value(binary_to_bcd_converter_1_p5));  // open: dp
  BCD8digits bcd8digits_1 (.BCD(bcd8digits_1_bcd), .Number(Res));
  Divider #(.width(32)) divider_1 (.a(R4), .b(R5), .out(divider_1_out), .rem(divider_1_rem));  // open: upper
  TTY tty_1 (.data(TTY_Char), .clk(Clk), .we(TTY_Upd), .clr(Reset));
  Multiplier #(.width(16)) multiplier_1 (.a(16'h2), .b(ROM_Addr), .out(multiplier_1_out));  // open: cin, cout
  // Probe on {MMIO_En, RAM_Addr, MMIO_Addr}
  // Probe on RAM_Out
  // Probe on CPU_1_sp
  Pull_Resistor pull_resistor_1 (.node(MMIO_Out));
  Multiplexer #(.enable("false"), .select(4), .width(32)) multiplexer_2 (
    .in0({undriven, TTY_Char}), .in1(Res), .in2(register_3_q), .in3(Dip1), .in4(Dip2), .in5(Dip3),
    .in6({undriven_2, KEYB_Eof}), .in7({undriven_3, KEYB_Char}), .in8({undriven_4, JOY_X}),
    .in9({undriven_5, JOY_Y}), .in10(random_1_out), .in11(bcd8digits_1_bcd), .in12(divider_1_out),
    .in13(divider_1_rem), .out(MMIO_Out), .sel(MMIO_Addr));  // open: in14, in15
  // Probe on multiplier_1_out
  and and_6 (and_6_out, ~Store, MMIO_En);  // AND_Gate
  Decoder #(.select(4)) decoder_2 (
    .out7(KEYB_Read), .out10(RNG_Read), .sel(MMIO_Addr), .en(and_6_out));  // open: out0, out1, out2, out3, out4, out5, out6, out8, out9, out11, out12, out13, out14, out15

  // Other names for the same wires on the sheet: RAM_Addr (some bits) = {MMIO_En, MMIO_Addr}

  // Notes on the sheet:
  //   Entrées / Sorties mappées en mémoire
  //   Sorties
  //   contents of ROMa (hex, n*v repeats v):
  //   b0ed b0ff b0f1 2003 340 9057 4*e7fe 2073 905d e7fe e7fe 2069 905d e7fe e7fe e7fe 206e 905d e7fe e7fe
  //   e7fe 2028 905d e7fe e7fe e7fe 9857 9056 9856 9008 9a08 10 c01 9155 9855 905e e7fe 9868 905c 985c b00
  //   905c 2000 905b 905a e7fe 985a 2804 d810 e7fe 985c 210f 4008 9059 985c 900 905c e7fe 9859 3030 905d
  //   e7fe e7fe 985a 1c40 905a e7e9 e7fe 9856 402 c12 2164 434a 434a c13 9355 9855 905e e7fe 202e 905d
  //   e7fe e7fe 9868 905c 985c c00 905c 2000 905b 905a e7fe 985a 2803 d810 e7fe 985c 210f 4008 9059 985c
  //   900 905c e7fe 9859 3030 905d e7fe e7fe 985a 1c40 905a e7e9 4*e7fe 2029 905d e7fe e7fe 203d 905d e7fe
  //   e7fe 20c9 280 9052 9852 213f 4308 9052 9852 9051 9851 9053 9857 9953 4 d 986a 904f 984f 9050 9850
  //   9953 849 4288 d904 e7fe 9853 9950 1a40 9050 e7fe 9850 904e 2001 400 904d 984e 904c 9850 a00 4340
  //   904b 2000 43c0 904a 2002 9049 e7fe 9849 280b d82b e7fe 984e a00 994b a09 4341 914e 984d a00 9949
  //   1c4a 9249 409 a09 4341 914d 984d a00 9949 409 a09 4341 914d 984a 994e 209 9a4d c 15 9969 9148 9948
  //   4348 200 994c 1808 904c e7fe 9849 1c40 9049 984a 4240 904a e7ce 984c 9047 9847 9054 e7fe 9854 9046
  //   9846 9007 9a07 10 c01 9145 9845 905e e7fe 9868 905c 985c b00 905c 2000 905b 905a e7fe 985a 2804 d810
  //   e7fe 985c 210f 4008 9059 985c 900 905c e7fe 9859 3030 905d e7fe e7fe 985a 1c40 905a e7e9 e7fe 9846
  //   402 c12 2164 434a 434a c13 9345 9845 905e e7fe 202e 905d e7fe e7fe 9868 905c 985c c00 905c 2000 905b
  //   905a e7fe 985a 2803 d810 e7fe 985c 210f 4008 9059 985c 900 905c e7fe 9859 3030 905d e7fe e7fe 985a
  //   1c40 905a e7e9 e7fe e7fe e7fe 200a 905d 5*e7fe 2063 905d e7fe e7fe 206f 905d e7fe e7fe e7fe 2073
  //   905d e7fe e7fe e7fe 2028 905d e7fe e7fe e7fe 9857 9044 9844 9006 9a06 10 c01 9143 9843 905e e7fe
  //   9868 905c 985c b00 905c 2000 905b 905a e7fe 985a 2804 d810 e7fe 985c 210f 4008 9059 985c 900 905c
  //   e7fe 9859 3030 905d e7fe e7fe 985a 1c40 905a e7e9 e7fe 9844 402 c12 2164 434a 434a c13 9343 9843
  //   905e e7fe 202e 905d e7fe e7fe 9868 905c 985c c00 905c 2000 905b 905a e7fe 985a 2803 d810 e7fe 985c
  //   210f 4008 9059 985c 900 905c e7fe 9859 3030 905d e7fe e7fe 985a 1c40 905a e7e9 4*e7fe 2029 905d e7fe
  //   e7fe 203d 905d e7fe e7fe 20c9 280 9040 9840 213f 4308 9040 9840 903f 983f 9041 9857 9941 4 d 986a
  //   903d 983d 903e 983e 9941 849 4288 d904 e7fe 9841 993e 1a40 903e e7fe 2001 401 913c 913b 993c 913a
  //   993e a09 4349 9139 2100 43c9 9138 9037 e7fe 9837 280b d82b e7fe 983c a00 9939 a09 4341 913c 983b a00
  //   9937 1c4a 9237 409 a09 4341 913b 983b a00 9937 409 a09 4341 913b 9838 993c 209 9a3b c 15 9969 9136
  //   9936 4348 200 993a 1808 903a e7fe 9837 1c40 9037 9838 4240 9038 e7ce 983a 9035 9835 9042 e7fe 9842
  //   9034 9834 9005 9a05 10 c01 9133 9833 905e e7fe 9868 905c 985c b00 905c 2000 905b 905a e7fe 985a 2804
  //   d810 e7fe 985c 210f 4008 9059 985c 900 905c e7fe 9859 3030 905d e7fe e7fe 985a 1c40 905a e7e9 e7fe
  //   9834 402 c12 2164 434a 434a c13 9333 9833 905e e7fe 202e 905d e7fe e7fe 9868 905c 985c c00 905c 2000
  //   905b 905a e7fe 985a 2803 d810 e7fe 985c 210f 4008 9059 985c 900 905c e7fe 9859 3030 905d e7fe e7fe
  //   985a 1c40 905a e7e9 e7fe e7fe e7fe 200a 905d e7fe e7fe 2001 400 9031 2002 9030 2000 902f e7fe 982f
  //   2801 d80a e7fe 9831 a00 9954 a09 4341 9131 e7fe 982f 1c40 902f e7ef 9831 902e 982e 2101 409 912d
  //   2102 912c 2100 912b 9004 e7fe 982b 2801 d80a e7fe 982d a00 9942 a09 4341 912d e7fe 982b 1c40 902b
  //   e7ef 982d 902a 982a 9904 1808 9032 9832 9003 9b03 18 c02 9229 9829 905e e7fe 9868 905c 985c b00 905c
  //   2000 905b 905a e7fe 985a 2804 d810 e7fe 985c 210f 4008 9059 985c 900 905c e7fe 9859 3030 905d e7fe
  //   e7fe 985a 1c40 905a e7e9 e7fe 9832 402 c12 2164 434a 434a c13 9329 9829 905e e7fe 202e 905d e7fe
  //   e7fe 9868 905c 985c c00 905c 2000 905b 905a e7fe 985a 2803 d810 e7fe 985c 210f 4008 9059 985c 900
  //   905c e7fe 9859 3030 905d e7fe e7fe 985a 1c40 905a e7e9 e7fe e7fe e7fe 200a 905d 5*e7fe 2074 905d
  //   e7fe e7fe 2061 905d e7fe e7fe e7fe 206e 905d e7fe e7fe e7fe 2028 905d e7fe e7fe e7fe 9857 9028 9828
  //   9002 9a02 10 c01 9127 9827 905e e7fe 9868 905c 985c b00 905c 2000 905b 905a e7fe 985a 2804 d810 e7fe
  //   985c 210f 4008 9059 985c 900 905c e7fe 98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
  //   Reprendre après un point d'arrêt
  //   Tic d'horloge
  //   Entrées
  //   PC effectif
endmodule

module CPU (
  input  [31:0] RAM_In,
  input  [15:0] ROM_In,
  input  Clk,
  input  Reset,
  output [31:0] R3,
  output [31:0] R7,
  output [31:0] R2,
  output [31:0] R6,
  output [31:0] R1,
  output [31:0] R5,
  output [31:0] R0,
  output [31:0] R4,
  output [31:0] RAM_Out,
  output [15:0] ROM_Addr,
  output [31:0] RAM_Addr,
  output Store,
  output [3:0] Flags,
  output [31:0] SP
);

  wire Controller_1_p7, Controller_1_p9, Controller_1_p11, Controller_1_p12, Controller_1_p13,
       Controller_1_p16, Controller_1_p17;
  wire [3:0] Controller_1_p4, Controller_1_p10;
  wire [4:0] Controller_1_p15, multiplexer_3_out;
  wire [31:0] ALU_1_s, Controller_1_p14, multiplexer_1_out, multiplexer_2_out, Regs_1_p15;

  Multiplexer #(.enable("false"), .width(32)) multiplexer_1 (
    .in0(ALU_1_s), .in1(RAM_In), .out(multiplexer_1_out), .sel(Controller_1_p7));
  // Controller Controller_1: pin names not known; wires that end beside it: ROM_In, Clk, Reset, Controller_1_p4, ROM_Addr, RAM_Addr, Controller_1_p7, Store, Controller_1_p9, Controller_1_p10, Controller_1_p11, Controller_1_p12, Controller_1_p13, Controller_1_p14, Controller_1_p15, Controller_1_p16, Controller_1_p17, Flags, SP
  // BancRegistre Regs_1: pin names not known; wires that end beside it: multiplexer_1_out, Controller_1_p11, Clk, R0, Reset, R1, R2, R3, R4, Controller_1_p12, R5, R6, Controller_1_p13, R7, Regs_1_p15, RAM_Out
  Multiplexer #(.enable("false"), .width(32)) multiplexer_2 (
    .in0(RAM_Out), .in1(Controller_1_p14), .out(multiplexer_2_out), .sel(Controller_1_p9));
  Multiplexer #(.enable("false"), .width(5)) multiplexer_3 (
    .in0(RAM_Out[4:0]), .in1(Controller_1_p15), .out(multiplexer_3_out), .sel(Controller_1_p16));
  ALU ALU_1 (
    .S(ALU_1_s), .Flags(Controller_1_p4), .A(multiplexer_2_out), .B(Regs_1_p15), .Shift(multiplexer_3_out),
    .CarryIn(Controller_1_p17), .Codop(Controller_1_p10));
endmodule

module BCD8digits (
  input  [31:0] Number,
  output [31:0] BCD
);

  wire [31:0] divider_1_out, divider_2_out, divider_3_out, divider_4_out, divider_5_out, divider_6_out,
       divider_7_out;
  wire [31:4] divider_1_rem, divider_2_rem, divider_3_rem, divider_4_rem, divider_5_rem, divider_6_rem,
       divider_7_rem, divider_8_rem;

  Divider #(.width(32)) divider_1 (
    .a(Number), .b(32'ha), .out(divider_1_out), .rem({divider_1_rem, BCD[31:28]}));  // open: upper
  Divider #(.width(32)) divider_2 (
    .a(divider_1_out), .b(32'ha), .out(divider_2_out), .rem({divider_2_rem, BCD[27:24]}));  // open: upper
  Divider #(.width(32)) divider_3 (
    .a(divider_2_out), .b(32'ha), .out(divider_3_out), .rem({divider_3_rem, BCD[23:20]}));  // open: upper
  Divider #(.width(32)) divider_4 (
    .a(divider_3_out), .b(32'ha), .out(divider_4_out), .rem({divider_4_rem, BCD[19:16]}));  // open: upper
  Divider #(.width(32)) divider_5 (
    .a(divider_4_out), .b(32'ha), .out(divider_5_out), .rem({divider_5_rem, BCD[15:12]}));  // open: upper
  Divider #(.width(32)) divider_6 (
    .a(divider_5_out), .b(32'ha), .out(divider_6_out), .rem({divider_6_rem, BCD[11:8]}));  // open: upper
  Divider #(.width(32)) divider_7 (
    .a(divider_6_out), .b(32'ha), .out(divider_7_out), .rem({divider_7_rem, BCD[7:4]}));  // open: upper
  Divider #(.width(32)) divider_8 (.a(divider_7_out), .b(32'ha), .rem({divider_8_rem, BCD[3:0]}));  // open: out, upper
  // Probe on BCD
endmodule
